# Fritzing sketch CouvertureChauffanteSchema (saved by Fritzing 0.8.7b)
breadboards: 1

parts:
  Composant1 = Arduino Uno (Rev3)
  LCD1 = LCD screen
  S1 = Pushbutton [package="[THT]"]
  S2 = Pushbutton [package="[THT]"]
  S3 = Pushbutton [package="[THT]"]
  S4 = Pushbutton [package="[THT]"]
  R1 = Resistor [tolerance=±5% resistance=220 package=THT]
  R2 = Resistor [tolerance=±5% resistance=10k package=THT]
  R3 = Resistor [tolerance=±5% resistance=10k package=THT]
  R4 = Resistor [tolerance=±5% resistance=10k package=THT]

nets:
  N1: Composant1.A0, S2.Pin_3, S2.Pin_4, R2.Pin_1
  N2: Composant1.D11_PWM/MOSI, LCD1.E
  N3: Composant1.D12/MISO, LCD1.RS
  N4: Composant1.D2, LCD1.DB7
  N5: Composant1.D3_PWM, LCD1.DB6
  N6: Composant1.D4, LCD1.DB5
  N7: Composant1.D5_PWM, LCD1.DB4
  N8: Composant1.D6_PWM, LCD1.V0
  5V: Composant1.5V, LCD1.VDD, R1.Pin_1
  GND: Composant1.GND, LCD1.VSS, LCD1.R/W, LCD1.LED-, S1.Pin_1, S1.Pin_2, S2.Pin_1, S2.Pin_2, S3.Pin_1, S3.Pin_2
  N9: LCD1.LED+, R1.Pin_0
  N10: S1.Pin_3, S1.Pin_4, R2.Pin_0, R4.Pin_1
  N11: S3.Pin_3, S3.Pin_4, R3.Pin_1, R4.Pin_0
  N12: S4.Pin_1, S4.Pin_2
  N13: S4.Pin_3, S4.Pin_4, R3.Pin_0
